// Logisim project auto_arm_proj.circ as structural Verilog: 6 circuits, main circuit auto_arm_simulation
module auto_arm_simulation (
);

  wire auto_arm_top_1_dest_blue_o, auto_arm_top_1_dest_init_o, auto_arm_top_1_dest_red_o,
       auto_arm_top_1_drop_o, auto_arm_top_1_move_o, auto_arm_top_1_scan_o, auto_arm_top_1_throw_o,
       clk_i_out, tclconsolereds_1_p23, tclconsolereds_1_p26;
  wire [1:0] tclconsolereds_1_p24;

  Clock clk_i (.out(clk_i_out));
  Clock sysclk ();  // open: out
  auto_arm_top auto_arm_top_1 (
    .ready_i(tclconsolereds_1_p23), .color_i(tclconsolereds_1_p24), .clk_i(clk_i_out),
    .reset_i(tclconsolereds_1_p26), .scan_o(auto_arm_top_1_scan_o), .throw_o(auto_arm_top_1_throw_o),
    .move_o(auto_arm_top_1_move_o), .dest_red_o(auto_arm_top_1_dest_red_o),
    .dest_blue_o(auto_arm_top_1_dest_blue_o), .dest_init_o(auto_arm_top_1_dest_init_o),
    .drop_o(auto_arm_top_1_drop_o));
  // TclConsoleReds #(.filePath("console\\console_auto_arm.tcl")) tclconsolereds_1: pin names not known; wires that end beside it: 4'b0000, 4'b0000, auto_arm_top_1_scan_o, auto_arm_top_1_throw_o, auto_arm_top_1_move_o, auto_arm_top_1_dest_red_o, auto_arm_top_1_dest_blue_o, auto_arm_top_1_dest_init_o, auto_arm_top_1_drop_o, 1'b0, 1'b0, 1'b0, 1'b0, 1'b0, 1'b0, 1'b0, 1'b0, 1'b0, {16{1'b0}}, {16{1'b0}}, {8{1'b0}}, clk_i_out, tclconsolereds_1_p23, tclconsolereds_1_p24[0], tclconsolereds_1_p24[1], tclconsolereds_1_p26

  // Notes on the sheet:
  //   Attention, votre version de Logisim
  //   ne contient pas de tracker. Si vous
  //   enregistrez votre projet, toutes les
  //   informations du tracker seront
  //   définitivement effacées.
endmodule

module auto_arm_top (
  input  ready_i,
  input  [1:0] color_i,
  input  clk_i,
  input  reset_i,
  output scan_o,
  output throw_o,
  output move_o,
  output dest_red_o,
  output dest_blue_o,
  output dest_init_o,
  output drop_o
);

  wire timer_1_end_timer_o;

  timer timer_1 (.nReset(move_o), .clk(clk_i), .end_timer_o(timer_1_end_timer_o));
  MSS mss_1 (
    .ready_i(ready_i), .color_i(color_i), .timer(timer_1_end_timer_o), .reset(reset_i), .clk(clk_i),
    .state({drop_o, dest_init_o, dest_blue_o, dest_red_o, move_o, throw_o, scan_o}));

  // Notes on the sheet:
  //   Attention, votre version de Logisim
  //   ne contient pas de tracker. Si vous
  //   enregistrez votre projet, toutes les
  //   informations du tracker seront
  //   définitivement effacées.
endmodule

module timer (
  input  nReset,
  input  clk,
  output end_timer_o
);

  wire not_1_out;

  Counter #(.width(2), .max('h2)) counter_1 (
    .clr(not_1_out), .clk(clk), .carry(end_timer_o));  // open: load, up, count, D, Q
  not not_1 (not_1_out, nReset);

  // Notes on the sheet:
  //   Attention, votre version de Logisim
  //   ne contient pas de tracker. Si vous
  //   enregistrez votre projet, toutes les
  //   informations du tracker seront
  //   définitivement effacées.
endmodule

module MSS (
  input  ready_i,
  input  [1:0] color_i,
  input  timer,
  input  reset,
  input  clk,
  output [6:0] state
);

  wire [2:0] decodeur_sorties_1_state_e_o;
  wire [6:0] decodeur_etat_1_next_state;

  decodeur_sorties decodeur_sorties_1 (.state_i(state), .state_E_o(decodeur_sorties_1_state_e_o));
  decodeur_etat decodeur_etat_1 (
    .state(decodeur_sorties_1_state_e_o), .ready_i(ready_i), .color_i(color_i), .timer(timer), .reset(reset),
    .next_state(decodeur_etat_1_next_state));
  D_Flip_Flop d_ff_1 (.D(decodeur_etat_1_next_state[5]), .clk(clk), .Q(state[5]));  // open: Qn, preset, reset
  D_Flip_Flop d_ff_2 (.D(decodeur_etat_1_next_state[4]), .clk(clk), .Q(state[4]));  // open: Qn, preset, reset
  D_Flip_Flop d_ff_3 (.D(decodeur_etat_1_next_state[3]), .clk(clk), .Q(state[3]));  // open: Qn, preset, reset
  D_Flip_Flop d_ff_4 (.D(decodeur_etat_1_next_state[2]), .clk(clk), .Q(state[2]));  // open: Qn, preset, reset
  D_Flip_Flop d_ff_5 (.D(decodeur_etat_1_next_state[1]), .clk(clk), .Q(state[1]));  // open: Qn, preset, reset
  D_Flip_Flop d_ff_6 (.D(decodeur_etat_1_next_state[0]), .clk(clk), .Q(state[0]));  // open: Qn, preset, reset
  D_Flip_Flop d_ff_7 (.D(decodeur_etat_1_next_state[6]), .clk(clk), .Q(state[6]));  // open: Qn, preset, reset

  // Notes on the sheet:
  //   Attention, votre version de Logisim
  //   ne contient pas de tracker. Si vous
  //   enregistrez votre projet, toutes les
  //   informations du tracker seront
  //   définitivement effacées.
endmodule

module decodeur_etat (
  input  [2:0] state,
  input  ready_i,
  input  [1:0] color_i,
  input  timer,
  input  reset,
  output [6:0] next_state
);

  wire [6:0] multiplexer_1_out, multiplexer_2_out, multiplexer_3_out, multiplexer_4_out, multiplexer_5_out,
       multiplexer_6_out;

  Multiplexer #(.select(2), .width(7), .enable("false")) multiplexer_1 (
    .in0(7'b0000010), .in1(7'b0001100), .in2(7'b0010100), .in3(7'b0000001), .out(multiplexer_1_out),
    .sel(color_i));
  Multiplexer #(.width(7), .enable("false")) multiplexer_2 (
    .in0(7'b0001100), .in1(7'b1000000), .out(multiplexer_2_out), .sel(timer));
  Multiplexer #(.width(7), .enable("false")) multiplexer_3 (
    .in0(7'b0010100), .in1(7'b1000000), .out(multiplexer_3_out), .sel(timer));
  Multiplexer #(.width(7), .enable("false")) multiplexer_4 (
    .in0(7'b0100100), .in1({7{1'b0}}), .out(multiplexer_4_out), .sel(timer));
  Multiplexer #(.width(7), .enable("false")) multiplexer_5 (
    .in0({7{1'b0}}), .in1(7'b0000001), .out(multiplexer_5_out), .sel(ready_i));
  Multiplexer #(.select(3), .width(7), .enable("false")) multiplexer_6 (
    .in0(multiplexer_5_out), .in1(multiplexer_1_out), .in2({7{1'b0}}), .in3(multiplexer_2_out),
    .in4(multiplexer_3_out), .in5(7'b0100100), .in6(multiplexer_4_out), .out(multiplexer_6_out), .sel(state));  // open: in7
  Multiplexer #(.width(7), .enable("false")) multiplexer_7 (
    .in0(multiplexer_6_out), .in1({7{1'b0}}), .out(next_state), .sel(reset));

  // Notes on the sheet:
  //   Attention, votre version de Logisim
  //   ne contient pas de tracker. Si vous
  //   enregistrez votre projet, toutes les
  //   informations du tracker seront
  //   définitivement effacées.
endmodule

module decodeur_sorties (
  input  [6:0] state_i,
  output [2:0] state_E_o
);

  wire nor_1_out, nor_2_out, nor_3_out, nor_4_out, nor_5_out, nor_6_out, nor_7_out, not_1_out, not_2_out,
       not_3_out, not_4_out, not_5_out, not_6_out, not_7_out, not_8_out, not_9_out;

  not not_1 (not_1_out, state_i[0]);
  not not_2 (not_2_out, state_i[1]);
  not not_3 (not_3_out, state_i[2]);
  not not_4 (not_4_out, state_i[3]);
  not not_5 (not_5_out, state_i[2]);
  not not_6 (not_6_out, state_i[4]);
  not not_7 (not_7_out, state_i[6]);
  not not_8 (not_8_out, state_i[2]);
  not not_9 (not_9_out, state_i[5]);
  nor nor_1 (nor_1_out, state_i[0], state_i[1], state_i[2], state_i[3], state_i[4], state_i[5], state_i[6]);
  nor nor_2 (nor_2_out, not_1_out, state_i[1], state_i[2], state_i[3], state_i[4], state_i[5], state_i[6]);
  nor nor_3 (nor_3_out, state_i[0], not_2_out, state_i[2], state_i[3], state_i[4], state_i[5], state_i[6]);
  nor nor_4 (nor_4_out, state_i[0], state_i[1], not_3_out, not_4_out, state_i[4], state_i[5], state_i[6]);
  nor nor_5 (nor_5_out, state_i[0], state_i[1], not_5_out, state_i[3], not_6_out, state_i[5], state_i[6]);
  nor nor_6 (nor_6_out, state_i[0], state_i[1], state_i[2], state_i[3], state_i[4], state_i[5], not_7_out);
  nor nor_7 (nor_7_out, state_i[0], state_i[1], not_8_out, state_i[3], state_i[4], not_9_out, state_i[6]);
  Priority_Encoder priority_encoder_1 (
    .in0(nor_1_out), .in1(nor_2_out), .in2(nor_3_out), .in3(nor_4_out), .in4(nor_5_out), .in5(nor_6_out),
    .in6(nor_7_out), .out(state_E_o));  // open: in7, en_in, gs, en_out

  // Notes on the sheet:
  //   Attention, votre version de Logisim
  //   ne contient pas de tracker. Si vous
  //   enregistrez votre projet, toutes les
  //   informations du tracker seront
  //   définitivement effacées.
endmodule
